// Logisim project PC.circ as structural Verilog: 1 circuit, main circuit main
module main (
);

  wire n74161_1_pin1, n74161_1_pin2, n74161_1_pin7, n74161_1_pin9, n74161_1_pin15, n74245_1_pin2,
       n74245_1_pin3, n74245_1_pin4, n74245_1_pin5, n74245_1_pin6, n74245_1_pin7, n74245_1_pin8,
       n74245_1_pin9, n74245_1_pin10, n74245_1_pin11, n74245_1_pin12, n74245_1_pin13, n74245_1_pin14,
       n74245_1_pin15, n74245_1_pin16, n74245_1_pin17, n74245_1_pin18, n74245_1_pin19, n74245_1_pin20;

  _74245 #(.ShowInternalStructure("true"), .VccGndPorts("true")) u_74245_1 (
    .pin2(n74245_1_pin2), .pin3(n74245_1_pin3), .pin4(n74245_1_pin4), .pin5(n74245_1_pin5),
    .pin6(n74245_1_pin6), .pin7(n74245_1_pin7), .pin8(n74245_1_pin8), .pin9(n74245_1_pin9),
    .pin10(n74245_1_pin10), .pin20(n74245_1_pin20), .pin19(n74245_1_pin19), .pin18(n74245_1_pin18),
    .pin17(n74245_1_pin17), .pin16(n74245_1_pin16), .pin15(n74245_1_pin15), .pin14(n74245_1_pin14),
    .pin13(n74245_1_pin13), .pin12(n74245_1_pin12), .pin11(n74245_1_pin11));  // open: pin1
  _74161 #(.ShowInternalStructure("true"), .VccGndPorts("true")) u_74161_1 (
    .pin1(n74161_1_pin1), .pin2(n74161_1_pin2), .pin3(n74245_1_pin18), .pin4(n74245_1_pin17),
    .pin5(n74245_1_pin16), .pin6(n74245_1_pin15), .pin7(n74161_1_pin7), .pin8(n74245_1_pin10),
    .pin16(n74245_1_pin20), .pin15(n74161_1_pin15), .pin14(n74245_1_pin2), .pin13(n74245_1_pin3),
    .pin12(n74245_1_pin4), .pin11(n74245_1_pin5), .pin10(n74161_1_pin7), .pin9(n74161_1_pin9));
  _74161 #(.ShowInternalStructure("true"), .VccGndPorts("true")) u_74161_2 (
    .pin1(n74161_1_pin1), .pin2(n74161_1_pin2), .pin3(n74245_1_pin14), .pin4(n74245_1_pin13),
    .pin5(n74245_1_pin12), .pin6(n74245_1_pin11), .pin7(n74161_1_pin7), .pin8(n74245_1_pin10),
    .pin16(n74245_1_pin20), .pin14(n74245_1_pin6), .pin13(n74245_1_pin7), .pin12(n74245_1_pin8),
    .pin11(n74245_1_pin9), .pin10(n74161_1_pin15), .pin9(n74161_1_pin9));  // open: pin15
endmodule
