// Logisim project test.alu.flag.circ as structural Verilog: 1 circuit, main circuit main
module main (
);

  wire CarryOut, n7404_1_pin5, n7408_1_pin3, n7408_1_pin5, n7408_1_pin6, n7408_1_pin8, n7408_1_pin11,
       n7408_1_pin12, n7408_1_pin13, n7432_1_pin3, n7432_1_pin4, n7432_1_pin11, n74161_1_pin1, n74161_1_pin2,
       n74161_1_pin3, n74161_1_pin4, n74161_1_pin5, n74161_1_pin6, n74161_1_pin7, n74161_1_pin9,
       n74161_1_pin10, n74161_1_pin11, n74161_1_pin12, n74161_1_pin13, n74161_1_pin14, n74161_1_pin15,
       n74181_1_p1, n74181_1_p2, n74181_1_p3, n74181_1_p4, n74181_1_p5, n74181_1_p6, n74181_1_p7,
       n74181_1_p8, n74181_1_p9, n74181_1_p10, n74181_1_p11, n74181_1_p12, n74181_1_p13, n74181_1_p14,
       n74181_1_p15, n74181_1_p17, n74181_1_p18, n74181_1_p20, n74181_1_p21, n74181_1_p22, n74181_1_p23, Zero;

  LED led_1 (.in(n74161_1_pin15));
  LED led_2 (.in(n74161_1_pin14));
  _74161 #(.ShowInternalStructure("true")) u_74161_1 (
    .pin1(n74161_1_pin1), .pin2(n74161_1_pin2), .pin3(n74161_1_pin3), .pin4(n74161_1_pin4),
    .pin5(n74161_1_pin5), .pin6(n74161_1_pin6), .pin7(n74161_1_pin7), .pin15(n74161_1_pin15),
    .pin14(n74161_1_pin14), .pin13(n74161_1_pin13), .pin12(n74161_1_pin12), .pin11(n74161_1_pin11),
    .pin10(n74161_1_pin10), .pin9(n74161_1_pin9));
  DipSwitch dipswitch_1 (
    .sw1(n74161_1_pin3), .sw2(n74161_1_pin4), .sw3(n74161_1_pin5), .sw4(n74161_1_pin6));  // open: sw5, sw6, sw7, sw8
  LED led_3 (.in(n74161_1_pin13));
  LED led_4 (.in(n74161_1_pin12));
  LED led_5 (.in(n74161_1_pin11));
  DipSwitch dipswitch_2 (
    .sw1(n74161_1_pin2), .sw2(n74161_1_pin1), .sw6(n74161_1_pin9), .sw7(n74161_1_pin7), .sw8(n74161_1_pin10));  // open: sw3, sw4, sw5
  // _74181 #(.ShowInternalStructure("true")) 74181_1: pin names not known; wires that end beside it: n74181_1_p1, n74181_1_p2, n74181_1_p3, n74181_1_p4, n74181_1_p5, n74181_1_p6, n74181_1_p7, n74181_1_p8, n74181_1_p9, n74181_1_p10, n74181_1_p11, n74181_1_p12, n74181_1_p13, n74181_1_p14, n74181_1_p15, CarryOut, n74181_1_p17, n74181_1_p18, n74181_1_p18, n74181_1_p20, n74181_1_p21, n74181_1_p22, n74181_1_p23
  _7404 #(.ShowInternalStructure("true")) u_7404_1 (
    .pin5(n7404_1_pin5), .pin6(Zero));  // open: pin1, pin2, pin3, pin4, pin13, pin12, pin11, pin10, pin9, pin8
  _7408 #(.ShowInternalStructure("true")) u_7408_1 (
    .pin1(n74181_1_p10), .pin2(n74181_1_p12), .pin3(n7408_1_pin3), .pin4(n7408_1_pin3), .pin5(n7408_1_pin5),
    .pin6(n7408_1_pin6), .pin13(n7408_1_pin13), .pin12(n7408_1_pin12), .pin11(n7408_1_pin11),
    .pin10(n7408_1_pin11), .pin9(n74181_1_p23), .pin8(n7408_1_pin8));
  DipSwitch #(.number(2)) dipswitch_3 (.sw1(n74181_1_p2), .sw2(n74181_1_p4));
  DipSwitch #(.number(2)) dipswitch_4 (.sw1(n74181_1_p6), .sw2(n74181_1_p8));
  DipSwitch #(.number(2)) dipswitch_5 (.sw1(n74181_1_p1), .sw2(n74181_1_p3));
  DipSwitch #(.number(4)) dipswitch_6 (.sw1(n74181_1_p5), .sw2(n74181_1_p7), .sw3(n74181_1_p9), .sw4(n74181_1_p11));
  _7404 #(.ShowInternalStructure("true")) u_7404_2 (
    .pin1(n74181_1_p10), .pin2(n7408_1_pin13), .pin3(n74181_1_p12), .pin4(n7408_1_pin12),
    .pin5(n74181_1_p23), .pin6(n7408_1_pin5));  // open: pin13, pin12, pin11, pin10, pin9, pin8
  LED led_6 (.in(n74181_1_p14));
  DipSwitch #(.number(2)) dipswitch_7 (.sw1(n74181_1_p10), .sw2(n74181_1_p12));
  DipSwitch #(.number(1)) dipswitch_8 (.sw1(n74181_1_p13));
  DipSwitch #(.number(1)) dipswitch_9 (.sw1(n74181_1_p15));
  LED led_7 (.in(Zero));
  LED led_8 (.in(CarryOut));
  LED led_9 ();  // open: in
  LED led_10 (.in(n74181_1_p21));
  LED led_11 (.in(n74181_1_p22));
  LED led_12 (.in(n74181_1_p20));
  LED led_13 (.in(n74181_1_p17));
  _7432 #(.ShowInternalStructure("true")) u_7432_1 (
    .pin1(n7408_1_pin8), .pin2(n7408_1_pin6), .pin3(n7432_1_pin3), .pin4(n7432_1_pin4), .pin5(n74181_1_p23),
    .pin6(n7404_1_pin5), .pin13(n74181_1_p17), .pin12(n74181_1_p20), .pin11(n7432_1_pin11),
    .pin10(n7432_1_pin11), .pin9(n74181_1_p22), .pin8(n7432_1_pin4));
  LED led_14 (.in(n7432_1_pin3));
  LED led_15 (.in(n74181_1_p23));
endmodule
